# Fritzing sketch schema (saved by Fritzing 0.9.3b)

parts:
  Part2 = 16-Channel 12-bit PCA9685 PWM/Servo Driver
  J1 = Basic Servo
  J2 = Basic Servo
  J5 = Basic Servo
  J6 = Basic Servo
  J3 = Basic Servo
  J4 = Basic Servo
  Part5 = Funduino JoyStick Shield 1.A
  Part3 = Arduino Leonardo (Rev3b)

nets:
  N1: Part2.0, J1.pulse
  N2: Part2.1, J2.pulse
  N3: Part2.2, J3.pulse
  N4: Part2.3, J4.pulse
  N5: Part2.4, J5.pulse
  GND: Part2.GND, J1.gnd, J2.gnd, J5.gnd, J6.gnd, J3.gnd, J4.gnd, Part3.GND
  N6: Part2.5, J6.pulse
  VCC: Part2.V+, J1.vcc, J2.vcc, J5.vcc, J6.vcc, J3.vcc, J4.vcc
  5V: Part2.VCC, Part5.5V, Part3.5V
  N7: Part2.SDA, Part3.SDA
  N8: Part2.SCL, Part3.SCL
  3.3V: Part5.3.3V, Part3.3V3
  N9: Part5.VERTICAL, Part3.A0
  N10: Part5.HORIZONTAL, Part3.A1
  N11: Part5.A2, Part3.A2
  N12: Part5.A3, Part3.A3
  N13: Part5.A4, Part3.A4
  N14: Part5.A5, Part3.A5
  N15: Part5.AREF, Part3.AREF
  N16: Part5.SEL, Part5.D9, Part3.D9_PWM/A9
  N17: Part5.D3, Part5.D10, Part3.D10_PWM/A10
  N18: Part5.D4, Part3.D4/A6
  N19: Part5.D5, Part3.D5_PWM
  N20: Part5.D6, Part3.D6_PWM/A7
  N21: Part5.D7, Part3.D7
  N22: Part5.D8, Part3.D8/A8
  N23: Part5.D11, Part3.D11_PWM
  N24: Part5.D12, Part3.D12/A11
  N25: Part5.D13, Part3.D13_PWM
  N26: Part5.RESET, Part3.RESET
  N27: Part5.RX, Part3.D0/RX
  N28: Part5.TX, Part3.D1/TX

custom parts:
  16-Channel 12-bit PCA9685 PWM/Servo Driver: The Adafruit 16-Channel 12-bit PWM/Servo Driver will drive up to 16 servos over I2C with only 2 pins. The on-board PCA9685 PWM controller will drive all 16 channels simultaneously with no additional processing overhead. What's more, you can chain up to 62 of them to control up to 992 servos - all with the same 2 pins
  Funduino JoyStick Shield 1.A: Description: The Joystick Shield sits on top of your Arduino and turns it into a simple controller. Five momentary push buttons (4+ joystick select button) and a two-axis thumb joystick gives your Arduino functionality on the level of old Nintendo controllers. Please note: This is an older version of the PCB that does not have the prototyping area. The examples and assembly guides still apply.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
